# Fritzing sketch robot (saved by Fritzing 0.9.6b)
circuit board: 4cm x 24cm
breadboards: 1

parts:
  HC-SR04 = mystery part, 4 pins [chip_label=?]
  GND_5V = Terminal 2pin
  L_motor = Terminal 2pin
  R_motor = Terminal 2pin
  PS2_Receiver = mystery part, 6 pins [chip_label=?]
  R1 = Resistor [tolerance=±5% power=0.25 resistance=5.6k package=THT]
  R2 = Resistor [tolerance=±5% power=0.25 resistance=5.6k package=THT]
  R3 = Resistor [tolerance=±5% power=0.25 resistance=5.6k package=THT]
  JDY-31_DIP = mystery part, 5 pins [chip_label=?]
  GND_5V_2 = Terminal 2pin
  C1 = Ceramic Capacitor [capacitance=100nF voltage=35V package="200 mil [THT, multilayer]"]
  C2 = Ceramic Capacitor [capacitance=100nF voltage=35V package="200 mil [THT, multilayer]"]
  Buzzer = mystery part, 5 pins [chip_label=?]
  GND_5V_3 = Terminal 2pin
  SDA_SCL = Terminal 2pin
  GY-BNO055 = mystery part, 8 pins [chip_label=?]
  Motor_Driver = Adafruit TB6612 DC and Stepper Motor Driver [part_number=TB6612]
  Arduino_Nano_Every = Arduino Nano Every

nets:
  5v: HC-SR04.pin1, GND_5V.pin_2, GND_5V_2.pin_1, GND_5V_3.pin_1, GY-BNO055.pin1, Motor_Driver.VCC, Arduino_Nano_Every.+5V
  N1: HC-SR04.pin2, Arduino_Nano_Every.D6~
  N2: HC-SR04.pin3, Arduino_Nano_Every.D5~
  GND: HC-SR04.pin4, GND_5V.pin_1, PS2_Receiver.pin3, JDY-31_DIP.pin5, GND_5V_2.pin_2, Buzzer.pin1, GND_5V_3.pin_2, GY-BNO055.pin2, Motor_Driver.GND#20, Arduino_Nano_Every.GND
  N3: L_motor.pin_1, C1.0, Motor_Driver.MOTORB2
  N4: L_motor.pin_2, C1.1, Motor_Driver.MOTORB1
  N5: R_motor.pin_1, C2.1, Motor_Driver.MOTORA1
  N6: R_motor.pin_2, C2.0, Motor_Driver.MOTORA2
  N7: PS2_Receiver.pin1, Arduino_Nano_Every.D12~/MISO
  N8: PS2_Receiver.pin2, R3.Pin_1
  3.3v: PS2_Receiver.pin4, JDY-31_DIP.pin4, Arduino_Nano_Every.3V3
  N9: PS2_Receiver.pin5, R1.Pin_1
  N10: PS2_Receiver.pin6, R2.Pin_1
  N11: R1.Pin_0, Arduino_Nano_Every.A0
  N12: R2.Pin_0, Arduino_Nano_Every.D13~
  N13: R3.Pin_0, Arduino_Nano_Every.D11/MOSI
  N14: JDY-31_DIP.pin2, Arduino_Nano_Every.RX
  N15: JDY-31_DIP.pin3, Arduino_Nano_Every.TX
  N16: Buzzer.pin2, Buzzer.pin3, Buzzer.pin4, Buzzer.pin5, Arduino_Nano_Every.A3
  SCL: SDA_SCL.pin_1, GY-BNO055.pin3, Arduino_Nano_Every.A5
  SDA: SDA_SCL.pin_2, GY-BNO055.pin4, Arduino_Nano_Every.A4
  N17: Motor_Driver.PWMB, Arduino_Nano_Every.D10~
  N18: Motor_Driver.BIN2, Arduino_Nano_Every.D8
  N19: Motor_Driver.BIN1, Arduino_Nano_Every.D7
  N20: Motor_Driver.AIN1, Arduino_Nano_Every.D4
  N21: Motor_Driver.AIN2, Arduino_Nano_Every.D2
  N22: Motor_Driver.PWMA, Arduino_Nano_Every.D9~

notes:
  eigenein/robot v2

custom parts:
  Terminal 2pin: 2-pin Terminal Block
  Adafruit TB6612 DC and Stepper Motor Driver: Spin two DC motors, step one bi-polar or uni-polar stepper, or fire off two solenoids with 1.2A per channel using the TB6612. These are perhaps better known as "the drivers in our assembled Adafruit Motorshield or Motor HAT." We really like these dual H-bridges, so if you want to control motors without a shield or HAT these are easy to include on any solderless breadboard or perma-proto.
  Arduino Nano Every: The Nano Every is Arduino’s 5V compatible board in the smallest available form factor: 45x18mm! The Arduino Nano is the preferred board for many projects requiring a small and easy to use microcontroller board. The small footprint and low price, make the Nano Every particularly suited for wearable inventions, low cost robotics, electronic musical instruments, and general use to control smaller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
