# Fritzing sketch robot (saved by Fritzing 0.9.6b)
circuit board: 4cm x 16cm
breadboards: 1

parts:
  Motor_Driver = Adafruit TB6612 DC and Stepper Motor Driver [part_number=TB6612]
  HMC5883L = Boladge HMC5883L Compass Module
  Piezo = Piezo Speaker
  HC-SR04 = mystery part, 4 pins [chip_label=?]
  V_logic = Terminal 2pin
  V_motors = Terminal 2pin
  L_motor = Terminal 2pin
  R_motor = Terminal 2pin
  Rotary = Terminal 2pin
  Arduino_Nano_Every = Arduino Nano Every
  C3 = Ceramic Capacitor [capacitance=100nF voltage=35V package="100 mil [THT, multilayer]"]
  C4 = Ceramic Capacitor [capacitance=100nF voltage=35V package="100 mil [THT, multilayer]"]
  C1 = Ceramic Capacitor [capacitance=100nF voltage=35V package="100 mil [THT, multilayer]"]
  C2 = Ceramic Capacitor [capacitance=100nF voltage=35V package="100 mil [THT, multilayer]"]

nets:
  N1: Motor_Driver.Vmotor, V_motors.pin_1
  GND: Motor_Driver.GND, HMC5883L.GND, Piezo.pin1, HC-SR04.pin4, V_logic.pin_1, V_motors.pin_2, Arduino_Nano_Every.GND, C3.0, C4.0
  VCC: Motor_Driver.VCC, HMC5883L.VCC, HC-SR04.pin1, V_logic.pin_2, Arduino_Nano_Every.+5V
  N2: Motor_Driver.PWMB, Arduino_Nano_Every.D10~
  N3: Motor_Driver.BIN2, Arduino_Nano_Every.D8
  N4: Motor_Driver.BIN1, Arduino_Nano_Every.D7
  N5: Motor_Driver.AIN1, Arduino_Nano_Every.D4
  N6: Motor_Driver.AIN2, Arduino_Nano_Every.D2
  N7: Motor_Driver.PWMA, Arduino_Nano_Every.D9~
  N8: Motor_Driver.MOTORA1, R_motor.pin_2, C2.1
  N9: Motor_Driver.MOTORA2, R_motor.pin_1, C2.0
  N10: Motor_Driver.MOTORB2, L_motor.pin_2, C1.0
  N11: Motor_Driver.MOTORB1, L_motor.pin_1, C1.1
  N12: HMC5883L.SCL, Arduino_Nano_Every.A5
  N13: HMC5883L.SDA, Arduino_Nano_Every.A4
  N14: Piezo.pin2, Arduino_Nano_Every.A3
  N15: HC-SR04.pin2, Arduino_Nano_Every.D6~
  N16: HC-SR04.pin3, Arduino_Nano_Every.D5~
  N17: Rotary.pin_1, Arduino_Nano_Every.A6, C4.1
  N18: Rotary.pin_2, Arduino_Nano_Every.A7, C3.1

notes:
  FRONT
  +
  L

custom parts:
  Adafruit TB6612 DC and Stepper Motor Driver: Spin two DC motors, step one bi-polar or uni-polar stepper, or fire off two solenoids with 1.2A per channel using the TB6612. These are perhaps better known as "the drivers in our assembled Adafruit Motorshield or Motor HAT." We really like these dual H-bridges, so if you want to control motors without a shield or HAT these are easy to include on any solderless breadboard or perma-proto.
  Boladge HMC5883L Compass Module: Cheap digital compass module
  Terminal 2pin: 2-pin Terminal Block
  Arduino Nano Every: The Nano Every is Arduino’s 5V compatible board in the smallest available form factor: 45x18mm! The Arduino Nano is the preferred board for many projects requiring a small and easy to use microcontroller board. The small footprint and low price, make the Nano Every particularly suited for wearable inventions, low cost robotics, electronic musical instruments, and general use to control smaller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
